// Logisim project alu.circ as structural Verilog: 1 circuit, main circuit ALU
module ALU (
  input  [7:0] A,
  input  [7:0] B,
  input  [2:0] S,
  output ZF,
  output [7:0] Out,
  output VF
);

  wire and_2_out, and_3_out, and_4_out, and_5_out, multiplexer_2_out, not_2_out, not_3_out, not_4_out,
       or_2_out, or_3_out, or_4_out, or_5_out, or_7_out, or_8_out, or_9_out;
  wire [7:0] and_1_out, multiplexer_1_out, multiplexer_3_out, multiplexer_4_out, not_1_out, or_1_out;

  assign and_1_out = A & B;  // AND_Gate and_1, 8 bits wide
  assign not_1_out = ~B;  // NOT_Gate not_1, 8 bits wide
  assign or_1_out = A | B;  // OR_Gate or_1, 8 bits wide
  Multiplexer #(.width(8)) multiplexer_1 (
    .in0(B), .in1(not_1_out), .out(multiplexer_1_out), .sel(multiplexer_2_out));  // open: en
  Multiplexer #(.select(3)) multiplexer_2 (
    .in0(1'b0), .in1(1'b0), .in2(1'b0), .in3(1'b0), .in4(1'b0), .in5(1'b1), .in6(1'b0), .in7(1'b0),
    .out(multiplexer_2_out), .sel(S));  // open: en
  Multiplexer #(.select(3), .width(8)) multiplexer_3 (
    .in0(A), .in1({8{1'b0}}), .in2(A), .in3(8'h1), .in4(A), .in5(A), .in6(and_1_out), .in7(or_1_out),
    .out(multiplexer_3_out), .sel(S));  // open: en
  Multiplexer #(.select(3), .width(8)) multiplexer_4 (
    .in0({8{1'b0}}), .in1(B), .in2(8'h1), .in3(B), .in4(B), .in5(multiplexer_1_out), .in6({8{1'b0}}),
    .in7({8{1'b0}}), .out(multiplexer_4_out), .sel(S));  // open: en
  not not_2 (not_2_out, multiplexer_3_out[7]);
  not not_3 (not_3_out, multiplexer_4_out[7]);
  Adder adder_1 (.a(multiplexer_3_out), .b(multiplexer_4_out), .out(Out), .cin(multiplexer_2_out));  // open: cout
  and and_2 (and_2_out, not_2_out, not_3_out);
  and and_3 (and_3_out, multiplexer_3_out[7], multiplexer_4_out[7]);
  and and_4 (and_4_out, Out[7], and_2_out);
  not not_4 (not_4_out, Out[7]);
  or or_2 (or_2_out, Out[0], Out[1]);
  and and_5 (and_5_out, and_3_out, not_4_out);
  or or_3 (or_3_out, Out[2], Out[3]);
  or or_4 (or_4_out, Out[4], Out[5]);
  or or_5 (or_5_out, Out[6], Out[7]);
  or or_6 (VF, and_4_out, and_5_out);
  or or_7 (or_7_out, or_2_out, or_3_out);
  or or_8 (or_8_out, or_4_out, or_5_out);
  or or_9 (or_9_out, or_7_out, or_8_out);
  not not_5 (ZF, or_9_out);
endmodule
